# Fritzing sketch drumminhands_pumpkin (saved by Fritzing 0.9.2b)
breadboards: 1

parts:
  neopixel1 = Neopixel Ring 16
  Part2 = Pro Trinket 5V
  R1 = Rotary Potentiometer (Large) [maximum_resistance=100kΩ package=THT]
  S1 = Momentary Switch [package=ksa_sealed_tac_switch]
  R2 = Resistor [tolerance=±5% resistance=220 package="0805 [SMD]"]
  VCC1 = Battery block 9V

nets:
  GND: neopixel1.GND, Part2.GND, R1.leg2, S1.2, VCC1.-
  VCC: neopixel1.VCC, Part2.+5V, R1.leg1
  N1: neopixel1.IN, R2.Pin_0
  N2: Part2.VBAT, VCC1.+
  N3: Part2.D6, R2.Pin_1
  N4: Part2.D4, S1.3
  N5: Part2.A0, R1.wiper

custom parts:
  Neopixel Ring 16: Neopixel Ring x16
  Pro Trinket 5V: The Pro Trinket 5V is like an Arduino Pro Mini with more pins and USB included. Built with the common core Arduino chip, the ATmega328p, it has 18 GPIO, 2 extra analog inputs, 28K of flash, and 2K of RAM. It has onboard USB bootloading support with Optiboot support, so you can either program your Pro Trinket over USB or with a FTDI cable. The Pro Trinket is programmable using the Arduino IDE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
